# Fritzing sketch schematic (saved by Fritzing 0.9.0b)
breadboards: 1

parts:
  LCD1 = LCD screen
  POT = Slide Potentiometer [maximum_resistance=10kΩ]
  R1 = Resistor [tolerance=±5% resistance=220 package=THT]

nets:
  GND: LCD1.VSS, LCD1.R/W, LCD1.LED-, POT.leg2
  5V: LCD1.VDD, POT.leg1, R1.Pin_0
  N1: LCD1.V0, POT.wiper
  D #12: LCD1.RS
  D #11: LCD1.E
  D #05: LCD1.DB4
  D #04: LCD1.DB5
  D #03: LCD1.DB6
  N2: LCD1.LED+, R1.Pin_1
