# Fritzing sketch schematic (saved by Fritzing 0.9.0b)
breadboards: 1

parts:
  U1 = 74HC595 [package="DIP16 [THT]"]
  7_Segment1 = 7 Segment Display
  R1 = Resistor [tolerance=±5% resistance=220 package=THT]
  R2 = Resistor [tolerance=±5% resistance=220 package=THT]
  R3 = Resistor [tolerance=±5% resistance=220 package=THT]
  R4 = Resistor [tolerance=±5% resistance=220 package=THT]
  R5 = Resistor [tolerance=±5% resistance=220 package=THT]
  R6 = Resistor [tolerance=±5% resistance=220 package=THT]
  R7 = Resistor [tolerance=±5% resistance=220 package=THT]
  R8 = Resistor [tolerance=±5% resistance=220 package=THT]

nets:
  N1: U1.Q1, R2.Pin_0
  N2: U1.Q2, R3.Pin_0
  N3: U1.Q3, R4.Pin_0
  N4: U1.Q4, R5.Pin_0
  N5: U1.Q5, R6.Pin_0
  N6: U1.Q6, R7.Pin_0
  N7: U1.Q7, R8.Pin_0
  GND: U1.GND, U1.OE, 7_Segment1.common_anode
  5V: U1.MR, U1.VCC
  D6: U1.SH_CP
  D5: U1.ST_CP
  D4: U1.DS
  N8: U1.Q0, R1.Pin_0
  N9: 7_Segment1.Segment_G, R7.Pin_1
  N10: 7_Segment1.Segment_F, R6.Pin_1
  N11: 7_Segment1.Segment_E, R5.Pin_1
  N12: 7_Segment1.Segment_D, R4.Pin_1
  N13: 7_Segment1.Segment_DP, R8.Pin_1
  N14: 7_Segment1.Segment_C, R3.Pin_1
  N15: 7_Segment1.Segment_B, R2.Pin_1
  N16: 7_Segment1.Segment_A, R1.Pin_1
