# Fritzing sketch schematic (saved by Fritzing 0.9.0b)
breadboards: 1

parts:
  U1 = 74HC595 [package="DIP16 [THT]"]
  R1 = Resistor [tolerance=±5% resistance=220 package=THT]
  R2 = Resistor [tolerance=±5% resistance=220 package=THT]
  R3 = Resistor [tolerance=±5% resistance=220 package=THT]
  R4 = Resistor [tolerance=±5% resistance=220 package=THT]
  R5 = Resistor [tolerance=±5% resistance=220 package=THT]
  R6 = Resistor [tolerance=±5% resistance=220 package=THT]
  R7 = Resistor [tolerance=±5% resistance=220 package=THT]
  R8 = Resistor [tolerance=±5% resistance=220 package=THT]
  LED1 = LED - 5mm [color="Red (633nm)" package="5 mm [THT]"]
  LED2 = LED - 5mm [color="Red (633nm)" package="5 mm [THT]"]
  LED3 = LED - 5mm [color="Red (633nm)" package="5 mm [THT]"]
  LED4 = LED - 5mm [color="Red (633nm)" package="5 mm [THT]"]
  LED5 = LED - 5mm [color="Red (633nm)" package="5 mm [THT]"]
  LED6 = LED - 5mm [color="Red (633nm)" package="5 mm [THT]"]
  LED7 = LED - 5mm [color="Red (633nm)" package="5 mm [THT]"]
  LED8 = LED - 5mm [color="Red (633nm)" package="5 mm [THT]"]

nets:
  N1: U1.Q1, R1.Pin_1
  N2: U1.Q2, R2.Pin_1
  N3: U1.Q3, R3.Pin_1
  N4: U1.Q4, R4.Pin_1
  N5: U1.Q5, R5.Pin_1
  N6: U1.Q6, R6.Pin_1
  N7: U1.Q7, R7.Pin_1
  GND: U1.GND, U1.OE, LED1.cathode, LED2.cathode, LED3.cathode, LED4.cathode, LED5.cathode, LED6.cathode, LED7.cathode, LED8.cathode
  5V: U1.MR, U1.VCC
  D6: U1.SH_CP
  D5: U1.ST_CP
  D4: U1.DS
  N8: U1.Q0, R8.Pin_0
  N9: R1.Pin_0, LED1.anode
  N10: R2.Pin_0, LED2.anode
  N11: R3.Pin_0, LED3.anode
  N12: R4.Pin_0, LED4.anode
  N13: R5.Pin_0, LED5.anode
  N14: R6.Pin_0, LED6.anode
  N15: R7.Pin_0, LED7.anode
  N16: R8.Pin_1, LED8.anode
