# Fritzing sketch schematic (saved by Fritzing 0.9.0b)
breadboards: 1

parts:
  R1 = Resistor [tolerance=±5% resistance=220 package=THT]
  R2 = Resistor [tolerance=±5% resistance=220 package=THT]
  R3 = Resistor [tolerance=±5% resistance=220 package=THT]
  RGB_LED = RGB LED (com. cathode, rbg) [package="5 mm [THT]"]

nets:
  D3~: R1.Pin_0
  N1: R1.Pin_1, RGB_LED.red_anode
  D5~: R2.Pin_0
  N2: R2.Pin_1, RGB_LED.blue_anode
  D6~: R3.Pin_0
  N3: R3.Pin_1, RGB_LED.green_anode
  GND: RGB_LED.common_cathode
