# Fritzing sketch schematic (saved by Fritzing 0.9.0b)
breadboards: 1

parts:
  M1 = DC Motor
  D1 = Rectifier Diode [part_number=1N4001 package="300 mil [THT]"]
  NPN = NPN-Transistor [package="TO92 [THT]"]
  R1 = Resistor [tolerance=±5% resistance=220 package=THT]

nets:
  5V: M1.pin_1, D1.cathode
  N1: M1.pin_2, D1.anode, NPN.C
  GND: NPN.E
  N2: NPN.B, R1.Pin_1
  D3: R1.Pin_0
