# Fritzing sketch leds_in_series (saved by Fritzing 0.9.0b)
breadboards: 1

parts:
  LED1 = LED - 5mm [color="Red (633nm)" package="5 mm [THT]"]
  LED2 = LED - 5mm [color="Red (633nm)" package="5 mm [THT]"]
  LED3 = LED - 5mm [color="Red (633nm)" package="5 mm [THT]"]
  R1 = Resistor [tolerance=±5% resistance=220 package=THT]

nets:
  5V: LED1.cathode
  N1: LED1.anode, LED2.cathode
  N2: LED2.anode, LED3.cathode
  N3: LED3.anode, R1.Pin_0
  GND: R1.Pin_1
