# Fritzing sketch schematic (saved by Fritzing 0.9.0b)
breadboards: 1

parts:
  Red = smd LED [color="Orange (605nm)" package="0805 [SMD]"]
  Blue = smd LED [color="Orange (605nm)" package="1206 [SMD]"]
  Green = smd LED [color="Orange (605nm)" package="1206 [SMD]"]
  Yellow = smd LED [color="Orange (605nm)" package="1206 [SMD]"]
  White = smd LED [color="Orange (605nm)" package="1206 [SMD]"]
  part = Resistor [tolerance=±5% resistance=220 package=THT]
  R3 = Resistor [tolerance=±5% resistance=220 package=THT]
  R4 = Resistor [tolerance=±5% resistance=220 package=THT]
  R5 = Resistor [tolerance=±5% resistance=220 package=THT]
  part_2 = Resistor [tolerance=±5% package="0402 [SMD]"]

nets:
  5V: Red.cathode, Blue.cathode, Green.cathode, Yellow.cathode, White.cathode
  N1: Red.anode, part_2.Pin_0
  N2: Blue.anode, part.Pin_0
  N3: Green.anode, R3.Pin_0
  N4: Yellow.anode, R4.Pin_0
  N5: White.anode, R5.Pin_0
  GND: part.Pin_1, R3.Pin_1, R4.Pin_1, R5.Pin_1, part_2.Pin_1

notes:
  Resistors
  LEDs
