# Fritzing sketch schematic (saved by Fritzing 0.9.0b)
breadboards: 1

parts:
  LM7805 = Voltage Regulator - 5V [package="TO220 [THT]"]
  C1 = Electrolytic Capacitor [capacitance=100µF package="100 mil [THT, electrolytic]"]
  C2 = Electrolytic Capacitor [capacitance=10µF package="100 mil [THT, electrolytic]"]
  LED1 = LED - 5mm [color="Red (633nm)" package="5 mm [THT]"]
  R1 = Resistor [tolerance=±5% resistance=220 package=THT]
  S1 = Toggle Switch [package=THT]
  V1 = DC Power [voltage=9]
  D1 = Rectifier Diode [part_number=1N4001 package="300 mil [THT]"]

nets:
  N1: LM7805.input_voltage, C1.+, S1.L2
  GND: LM7805.GND, C1.-, C2.-, R1.Pin_0, V1.V-
  N2: LM7805.output_voltage, C2.+, LED1.anode
  N3: LED1.cathode, R1.Pin_1
  N4: S1.COM, D1.cathode
  N5: V1.V+, D1.anode

notes:
  5V
  9V
