# Fritzing sketch schematic (saved by Fritzing 0.9.0b)
breadboards: 1

parts:
  R1 = Resistor [tolerance=±5% resistance=220 package=THT]
  R2 = Resistor [tolerance=±5% resistance=220 package=THT]
  R3 = Resistor [tolerance=±5% resistance=220 package=THT]
  R4 = Resistor [tolerance=±5% resistance=220 package=THT]
  5V = DC Power [voltage=5]
  S1 = Pushbutton [package=THT]
  S2 = Pushbutton [package=THT]
  Q1 = NPN-Transistor [package="TO92 [THT]"]
  LED1 = LED - 5mm [color="Red (633nm)" package="5 mm [THT]"]
  Q2 = NPN-Transistor [package="TO92 [THT]"]
  LED2 = LED - 5mm [color="Red (633nm)" package="5 mm [THT]"]

nets:
  N1: R1.Pin_0, S1.leg1
  N2: R1.Pin_1, R2.Pin_1, R3.Pin_1, R4.Pin_1, 5V.V+
  N3: R2.Pin_0, LED1.anode
  N4: R3.Pin_0, S2.leg1
  N5: R4.Pin_0, Q2.C, LED2.anode
  N6: 5V.V-, Q1.E, Q2.E, LED2.cathode
  N7: S1.leg0, Q1.B
  N8: S2.leg0, Q2.B
  N9: Q1.C, LED1.cathode
