# Fritzing sketch schematic (saved by Fritzing 0.9.0b)
breadboards: 1

parts:
  NPN = NPN-Transistor [package="TO92 [THT]"]
  R1 = Resistor [tolerance=±5% resistance=10 package=THT]
  LED_(red) = LED - 5mm [color="Red (633nm)" package="5 mm [THT]"]
  LDR = Photocell (LDR) [package=THT]
  R2 = Resistor [tolerance=±5% resistance=10k package=THT]

nets:
  5V: NPN.E, R2.Pin_1
  N1: NPN.B, LDR.pin_1, R2.Pin_0
  N2: NPN.C, R1.Pin_1
  N3: R1.Pin_0, LED_(red).anode
  GND: LED_(red).cathode, LDR.pin_0
