# Fritzing sketch schematic (saved by Fritzing 0.9.0b)
breadboards: 1

parts:
  S1 = Pushbutton [package=THT]
  S2 = Pushbutton [package=THT]
  Q1 = NPN-Transistor [package="TO92 [THT]"]
  Q2 = NPN-Transistor [package="TO92 [THT]"]
  R1 = Resistor [tolerance=±5% resistance=220 package=THT]
  R2 = Resistor [tolerance=±5% resistance=220 package=THT]
  LED1 = LED - 5mm [color="Red (633nm)" package="5 mm [THT]"]
  R3 = Resistor [tolerance=±5% resistance=220 package=THT]
  5V = DC Power [voltage=5]
  Q3 = NPN-Transistor [package="TO92 [THT]"]
  Q4 = NPN-Transistor [package="TO92 [THT]"]
  S3 = Pushbutton [package=THT]
  S4 = Pushbutton [package=THT]
  LED2 = LED - 5mm [color="Red (633nm)" package="5 mm [THT]"]
  R4 = Resistor [tolerance=±5% resistance=220 package=THT]
  R5 = Resistor [tolerance=±5% resistance=220 package=THT]
  R6 = Resistor [tolerance=±5% resistance=220 package=THT]
  5V_2 = DC Power [voltage=5]

nets:
  N1: S1.leg0, Q1.B
  N2: S1.leg1, R1.Pin_1
  N3: S2.leg0, Q2.B
  N4: S2.leg1, R2.Pin_1
  N5: Q1.E, Q2.C
  N6: Q1.C, LED1.cathode
  N7: Q2.E, 5V.V-
  N8: R1.Pin_0, R2.Pin_0, R3.Pin_0, 5V.V+
  N9: LED1.anode, R3.Pin_1
  N10: Q3.E, Q4.E, 5V_2.V-
  N11: Q3.B, S4.leg0
  N12: Q3.C, Q4.C, LED2.cathode
  N13: Q4.B, S3.leg0
  N14: S3.leg1, R5.Pin_1
  N15: S4.leg1, R6.Pin_1
  N16: LED2.anode, R4.Pin_1
  N17: R4.Pin_0, R5.Pin_0, R6.Pin_0, 5V_2.V+
