# Fritzing sketch schematic (saved by Fritzing 0.9.0b)
breadboards: 1

parts:
  Q1 = NPN-Transistor [package="TO92 [THT]"]
  Q2 = NPN-Transistor [package="TO92 [THT]"]
  Q3 = NPN-Transistor [package="TO92 [THT]"]
  Q4 = NPN-Transistor [package="TO92 [THT]"]
  Q5 = NPN-Transistor [package="TO92 [THT]"]
  LED = LED - 5mm [color="Red (633nm)" package="5 mm [THT]"]
  R1 = Resistor [tolerance=±5% resistance=220 package=THT]
  S1 = Pushbutton [package=THT]
  S2 = Pushbutton [package=THT]
  R2 = Resistor [tolerance=±5% resistance=220 package=THT]
  R3 = Resistor [tolerance=±5% resistance=220 package=THT]
  R4 = Resistor [tolerance=±5% resistance=220 package=THT]
  R5 = Resistor [tolerance=±5% resistance=220 package=THT]
  R4_2 = Resistor [tolerance=±5% resistance=220 package=THT]

nets:
  N1: Q1.E, Q2.C
  N2: Q1.B, Q4.B, S1.leg1
  GND: Q1.C, Q3.C
  N3: Q2.E, R4.Pin_0, R5.Pin_0
  N4: Q2.B, Q5.B, S2.leg1
  N5: Q3.E, Q4.C, Q5.C, R5.Pin_1, R4_2.Pin_0
  N6: Q3.B, R4.Pin_1
  N7: Q4.E, Q5.E, LED.cathode
  N8: LED.anode, R1.Pin_1
  5V: R1.Pin_0, R2.Pin_1, R3.Pin_1, R4_2.Pin_1
  N9: S1.leg0, R2.Pin_0
  N10: S2.leg0, R3.Pin_0
