# Fritzing sketch nand (saved by Fritzing 0.9.0b)
breadboards: 1

parts:
  T2 = NPN-Transistor [package="TO92 [THT]"]
  T1 = NPN-Transistor [package="TO92 [THT]"]
  L1 = LED - 5mm [color="Red (633nm)" package="5 mm [THT]"]
  S1 = Pushbutton [package=THT]
  S2 = Pushbutton [package=THT]
  R1 = Resistor [tolerance=±5% resistance=220 package=THT]
  R2 = Resistor [tolerance=±5% resistance=220 package=THT]
  R3 = Resistor [tolerance=±5% resistance=220 package=THT]

nets:
  N1: T2.E, T1.C
  N2: T2.B, S1.leg1
  N3: T2.C, L1.anode, R1.Pin_1
  GND: T1.E, L1.cathode
  N4: T1.B, S2.leg1
  N5: S1.leg0, R2.Pin_1
  N6: S2.leg0, R3.Pin_1
  5V: R1.Pin_0, R2.Pin_0, R3.Pin_0
